# Fritzing sketch prototype (saved by Fritzing 0.7.12b)
breadboards: 2

parts:
  Teensy1 = Teensy 2.0
  IC1 = DS1621 [package="DIP8 [THT]"]

nets:
  N1: Teensy1.D0, IC1.SDA
  N2: Teensy1.D1, IC1.SCL

custom parts:
  DS1621: DS1621 I2C Temperatire Sensor
